# Fritzing sketch schematic (saved by Fritzing 0.9.3b)
breadboards: 1

parts:
  Part1 = Intel Galileo
  S1 = Pushbutton [package=THT]
  R1 = Resistor [tolerance=±5% resistance=330 package=THT]
  LED1 = LED - 5mm [color="Red (633nm)" package="5 mm [THT]"]
  LED2 = LED - 5mm [color="Blue (525nm)" package="5 mm [THT]"]
  R2 = Resistor [tolerance=±5% resistance=330 package=THT]
  R3 = Resistor [tolerance=±5% resistance=220 package=THT]

nets:
  N1: Part1.D12/MISO, R2.Pin_0
  N2: Part1.D13/SCK, R3.Pin_0
  N3: Part1.GND, R1.Pin_1, LED1.cathode, LED2.cathode
  N4: Part1.5V, S1.leg0
  N5: S1.leg1, R1.Pin_0
  N6: LED1.anode, R2.Pin_1
  N7: LED2.anode, R3.Pin_1
