# Fritzing sketch schematic (saved by Fritzing 0.9.3b)
breadboards: 1

parts:
  LED1 = RGB LED (com. cathode, rgb) [package="5 mm [THT]"]
  R1 = Photocell (LDR) [package=THT]
  Part1 = Arduino Uno (Rev3)
  R2 = Resistor [tolerance=±5% resistance=330 package=THT]
  R3 = Resistor [tolerance=±5% resistance=330 package=THT]
  R4 = Resistor [tolerance=±5% resistance=330 package=THT]

nets:
  N1: LED1.red_anode, R3.Pin_1
  N2: LED1.common_cathode, R1.pin_1, Part1.GND
  N3: LED1.blue_anode, R4.Pin_1
  N4: R1.pin_0, Part1.A0, R2.Pin_1
  N5: Part1.D9_PWM, R3.Pin_0
  N6: Part1.D10_PWM/SS, R4.Pin_0
  N7: Part1.5V, R2.Pin_0
