# Fritzing sketch schematic (saved by Fritzing 0.9.3b)
breadboards: 1

parts:
  Q1 = NPN-Transistor [package="TO92 [THT]"]
  R1 = Resistor [tolerance=±5% resistance=330 package=THT]
  R2 = Photocell (LDR) [package=THT]
  R3 = Resistor [tolerance=±5% resistance=330 package=THT]
  LED1 = LED - 5mm [color="White (4500K)" package="5 mm [THT]"]  # not connected
  LED2 = LED - 5mm [color="White (4500K)" package="5 mm [THT]"]  # not connected
  LED3 = LED - 5mm [color="White (4500K)" package="5 mm [THT]"]
  R4 = Resistor [tolerance=±5% resistance=240 package=THT]
  R5 = Resistor [tolerance=±5% resistance=240 package=THT]
  Part1 = Arduino Uno (Rev3)
  LED4 = LED - 5mm [color="White (4500K)" package="5 mm [THT]"]  # not connected
  LED5 = LED - 5mm [color="White (4500K)" package="5 mm [THT]"]  # not connected
  LED6 = LED - 5mm [color="White (4500K)" package="5 mm [THT]"]  # not connected
  V1 = DC Power [voltage=12V]

nets:
  N1: Q1.E, R2.pin_0, Part1.GND, V1.V-
  N2: Q1.C, LED3.cathode
  N3: R1.Pin_0, Part1.D11_PWM/MOSI
  N4: R2.pin_1, R3.Pin_0, Part1.A0
  N5: R3.Pin_1, Part1.5V
  N6: R4.Pin_1, R5.Pin_1, V1.V+
