# Fritzing sketch schematic (saved by Fritzing 0.9.3b)
breadboards: 1

parts:
  Part1 = Arduino Uno (Rev3)
  Part2 = Thumb Joystick
  J1 = Basic Servo

nets:
  N1: Part1.A4/SDA, Part2.HORZ
  N2: Part1.A5/SCL, Part2.VERT
  N3: Part1.D13/SCK, Part2.SEL
  N4: Part1.D6_PWM, J1.pulse
  GND: Part1.GND, Part2.GND, J1.gnd
  VCC: Part2.VCC, J1.vcc
