# Fritzing sketch schematic (saved by Fritzing 0.9.3b)
breadboards: 1

parts:
  Arduino = Arduino Uno (Rev3)
  R1 = Resistor [tolerance=±5% resistance=330 package=THT]
  R2 = Photocell (LDR) [package=THT]

nets:
  N1: Arduino.GND, R2.pin_1
  N2: Arduino.5V, R1.Pin_0
  N3: R1.Pin_1, R2.pin_0
