# Fritzing sketch schematic (saved by Fritzing 0.9.3b)
breadboards: 1

parts:
  Arduino = Arduino Uno (Rev3)
  R1 = Resistor [tolerance=±5% resistance=330 package=THT]
  R2 = Resistor [tolerance=±5% resistance=330 package=THT]
  R3 = Rotary Potentiometer (Small) [maximum_resistance=100kΩ package=THT]
  Q1 = NPN-Transistor [package="TO92 [THT]"]
  LED1 = LED - 5mm [color="White (4500K)" package="5 mm [THT]"]
  LED2 = LED - 5mm [color="White (4500K)" package="5 mm [THT]"]
  LED3 = LED - 5mm [color="White (4500K)" package="5 mm [THT]"]
  R4 = Resistor [tolerance=±5% resistance=220 package=THT]
  LED4 = LED - 5mm [color="White (4500K)" package="5 mm [THT]"]
  LED5 = LED - 5mm [color="White (4500K)" package="5 mm [THT]"]
  LED6 = LED - 5mm [color="White (4500K)" package="5 mm [THT]"]
  R5 = Resistor [tolerance=±5% resistance=220 package=THT]
  V1 = DC Power [voltage=12V]
  R6 = Photocell (LDR) [package=THT]

nets:
  N1: Arduino.A0, R2.Pin_0, R6.pin_1
  N2: Arduino.A5/SCL, R3.leg2
  N3: Arduino.D11_PWM/MOSI, R1.Pin_0
  N4: Arduino.GND, R3.wiper, Q1.E, V1.V-, R6.pin_0
  N5: Arduino.5V, R2.Pin_1, R3.leg1
  N6: R1.Pin_1, Q1.B
  N7: Q1.C, LED3.cathode, LED6.cathode
  N8: LED1.cathode, LED2.anode
  N9: LED1.anode, R4.Pin_0
  N10: LED2.cathode, LED3.anode
  N11: R4.Pin_1, V1.V+
  N12: LED4.cathode, LED5.anode
  N13: LED4.anode, R5.Pin_0
  N14: LED5.cathode, LED6.anode
